# Fritzing sketch scheme (saved by Fritzing 0.9.4)
breadboards: 1

parts:
  Компонент1 = Arduino Nano (Rev3.0)
  S1 = Pushbutton [package="[THT]"]
  S2 = Pushbutton [package="[THT]"]
  S3 = Pushbutton [package="[THT]"]
  LED1 = LED - 5mm [color="Red (633nm)" package="5 mm [THT]"]
  LED2 = LED - 5mm [color="Yellow (595nm)" package="5 mm [THT]"]
  LED3 = LED - 5mm [color="Green (570nm)" package="5 mm [THT]"]
  R1 = Resistor [tolerance=±5% resistance=220 package=THT]
  R2 = Resistor [tolerance=±5% resistance=220 package=THT]
  R3 = Resistor [tolerance=±5% resistance=220 package=THT]

nets:
  N1: Компонент1.GND, Компонент1.D2, Компонент1.D3, Компонент1.D4, S1.Pin_3, S1.Pin_4, S2.Pin_3, S2.Pin_4, S3.Pin_3, S3.Pin_4, LED1.cathode, LED2.cathode, LED3.cathode
  N2: Компонент1.D8, R1.Pin_0
  N3: Компонент1.D9, R2.Pin_0
  N4: Компонент1.D10, R3.Pin_0
  N5: S1.Pin_1, S1.Pin_2
  N6: S2.Pin_1, S2.Pin_2
  N7: S3.Pin_1, S3.Pin_2
  N8: LED1.anode, R1.Pin_1
  N9: LED2.anode, R2.Pin_1
  N10: LED3.anode, R3.Pin_1
